// Logisim project MIPS.circ as structural Verilog: 17 circuits, main circuit CPU
module CPU (
  input  run
);

  wire aj, and_1_out, and_2_out, branchunit_1_out_11, cin, clk, flagie, hit, hit_2_q, hit_q, imm, j, jrt,
       multiplexer_11_out, not_1_out, or_1_out, or_2_out, or_3_out, res, shj, st, taken, we, zero;
  wire [0:0] ctrl_4_q;
  wire [1:0] ctrl_4_q_2, dest, dest_2_q, dest_q, fA, fB, forwardsel_1_out_2, forwardsel_2_out_2,
       forwardsel_3_out_2, jmp, oldD, R1, sel, wb_t;
  wire [3:0] flag, FLAGS_q;
  wire [5:0] par1_q;
  wire [5:3] ctrl_2_q;
  wire [7:0] A, A_2_q, A_q, add, adder_1_out, alu8bit_1_aluout, aluO, ALUout_2_q, B, B_2_q, B_3_q, B_q,
       branchunit_1_address, data, EX, iAddr, iAddr_2_q, iAddr_q, IR1_q, jr, M, M_2_q, M_q, MEM,
       multiplexer_1_out, multiplexer_2_out, multiplexer_3_out, multiplexer_4_out, multiplexer_5_out,
       multiplexer_5_out_2, multiplexer_6_out, multiplexer_7_out, nextAdd, op, op2_2_q, op2_q, p2, PC_q,
       register_1_q, register_2_q, registerset_1_al, registerset_1_bl, registerset_1_cl, registerset_1_dl,
       registerset_1_r1, registerset_1_r2, WB;
  wire [11:0] controlunit_1_out_2;
  wire [11:6] ctrl_q;
  wire [15:0] IR2_q;
  wire [23:0] ram_1_data;

  Multiplexer #(.select(2), .width(8), .enable("false")) multiplexer_1 (
    .in0(multiplexer_3_out), .in1(add), .in2(nextAdd), .in3(nextAdd), .out(multiplexer_1_out), .sel({shj, aj}));
  Register PC (.D(multiplexer_1_out), .en(run), .Q(PC_q), .clk(clk), .clr(res));
  Clock Clock (.out(clk));
  Button Reset (.out(res));
  Multiplexer #(.width(8), .enable("false")) multiplexer_2 (
    .in0(multiplexer_4_out), .in1(multiplexer_5_out_2), .out(multiplexer_2_out), .sel(branchunit_1_out_11));
  Multiplexer #(.width(8), .enable("false")) multiplexer_3 (
    .in0(multiplexer_2_out), .in1(A), .out(multiplexer_3_out), .sel(jrt));
  Adder adder_1 (.a(8'h1), .b(PC_q), .out(adder_1_out));  // open: cin, cout
  BranchUnit branchunit_1 (
    .pc(iAddr_q), .res(res), .clk(clk), .in_5({add, iAddr}), .update(j), .hit(hit),
    .address(branchunit_1_address), .op(op), .out_11(branchunit_1_out_11), .jmp(jmp), .out_12(jrt), .jr(jr));
  Multiplexer #(.width(8), .enable("false")) multiplexer_4 (
    .in0(adder_1_out), .in1(branchunit_1_address), .out(multiplexer_4_out), .sel(hit));
  RAM #(.dataWidth(24)) ram_1 (.addr(PC_q), .data(ram_1_data), .ld(1'b1));  // open: sel, clk, clr
  Multiplexer #(.width(24), .enable("false")) multiplexer_5 (
    .in0(ram_1_data), .in1({24{1'b0}}), .out({op, multiplexer_5_out_2, multiplexer_5_out}), .sel(or_1_out));
  or or_1 (or_1_out, and_1_out, jrt, taken);
  and and_1 (and_1_out, ~aj, hit);  // AND_Gate
  Register u_iAddr (.D(PC_q), .en(run), .Q(iAddr_q), .clk(clk), .clr(or_2_out));
  Register #(.width(16)) IR2 (
    .D({multiplexer_5_out_2, multiplexer_5_out}), .en(run), .Q(IR2_q), .clk(clk), .clr(or_2_out));
  Register IR1 (.D(op), .en(run), .Q(IR1_q), .clk(clk), .clr(or_2_out));
  or or_2 (or_2_out, res, jrt, taken);
  // Probe on registerset_1_al
  // Probe on registerset_1_bl
  // Probe on registerset_1_dl
  // Probe on registerset_1_cl
  RegisterSet registerset_1 (
    .DataIn(data), .WE(we), .R1sel(IR2_q[15:14]), .R2sel(IR2_q[7:6]), .R1(registerset_1_r1),
    .R2(registerset_1_r2), .Reset(res), .AL(registerset_1_al), .BL(registerset_1_bl), .CL(registerset_1_cl),
    .DL(registerset_1_dl), .clk(clk), .dest(dest));
  ControlUnit controlunit_1 (.opcode(IR1_q), .out_2(controlunit_1_out_2));
  Register #(.width(1)) u_hit (.D(hit), .en(run), .Q(hit_q), .clk(clk), .clr(or_3_out));
  Register iAddr_2 (.D(iAddr_q), .en(run), .Q(iAddr_2_q), .clk(clk), .clr(or_3_out));
  Register par1 (.D(IR2_q[15:8]), .en(run), .Q({R1, par1_q}), .clk(clk), .clr(or_3_out));
  Register par2 (.D(IR2_q[7:0]), .en(run), .Q(p2), .clk(clk), .clr(or_3_out));
  Register u_A (.D(registerset_1_r1), .en(run), .Q(A_q), .clk(clk), .clr(or_3_out));
  Register u_B (.D(registerset_1_r2), .en(run), .Q(B_q), .clk(clk), .clr(or_3_out));
  Register opcode (.D(IR1_q), .en(run), .Q(jr), .clk(clk), .clr(or_3_out));
  Register #(.width(2)) u_dest (.D(IR2_q[15:14]), .en(run), .Q(dest_q), .clk(clk), .clr(or_3_out));
  Register #(.width(12)) ctrl (
    .D(controlunit_1_out_2), .en(run), .Q({ctrl_q, sel, cin, zero, imm, flagie}), .clk(clk), .clr(or_3_out));
  or or_3 (or_3_out, res, taken);
  Multiplexer #(.width(8), .enable("false")) multiplexer_6 (
    .in0(A_q), .in1({8{1'b0}}), .out(multiplexer_6_out), .sel(zero));
  Multiplexer #(.width(8), .enable("false")) multiplexer_7 (.in0(B_q), .in1(p2), .out(multiplexer_7_out), .sel(imm));
  Multiplexer #(.select(2), .width(8), .enable("false")) multiplexer_8 (
    .in0(multiplexer_6_out), .in1(EX), .in2(MEM), .in3(WB), .out(A), .sel(fA));
  Multiplexer #(.select(2), .width(8), .enable("false")) multiplexer_9 (
    .in0(WB), .in1(MEM), .in2(EX), .in3(multiplexer_7_out), .out(B), .sel(fB));
  ForwardingUnit forwardingunit_1 (
    .zero(zero), .R1(R1), .dest1(dest_2_q), .we1(ctrl_2_q[3]), .R2(p2[7:6]), .imm(imm), .fA(fA),
    .dest2(dest), .we2(we), .wb1(ctrl_2_q[5:4]), .wb2(wb_t), .dest3(oldD), .we3(ctrl_4_q[0]), .fB(fB),
    .wb3(ctrl_4_q_2));
  and and_2 (and_2_out, flagie, run);
  ALU8bit alu8bit_1 (.B(B), .A(A), .ALUout(alu8bit_1_aluout), .FLAGS(flag), .Cin(cin), .Sel(sel));
  Register #(.width(1)) hit_2 (.D(hit_q), .en(run), .Q(hit_2_q), .clk(clk), .clr(res));
  Register iAddr_3 (.D(iAddr_2_q), .en(run), .Q(iAddr), .clk(clk), .clr(res));
  Register address (.D({R1, par1_q}), .en(run), .Q(add), .clk(clk), .clr(res));
  Register #(.width(4)) FLAGS (.D(flag), .en(and_2_out), .Q(FLAGS_q), .clk(clk), .clr(res));
  Register op2 (.D(p2), .en(run), .Q(op2_q), .clk(clk), .clr(res));
  Register ALUout (.D(alu8bit_1_aluout), .en(run), .Q(aluO), .clk(clk), .clr(res));
  Register A_2 (.D(A), .en(run), .Q(A_2_q), .clk(clk), .clr(res));
  Register B_2 (.D(B), .en(run), .Q(B_2_q), .clk(clk), .clr(res));
  Register #(.width(2)) dest_2 (.D(dest_q), .en(run), .Q(dest_2_q), .clk(clk), .clr(res));
  Register #(.width(6)) ctrl_2 (.D(ctrl_q), .en(run), .Q({ctrl_2_q, st, jmp}), .clk(clk), .clr(res));
  Adder adder_2 (.a(8'h1), .b(iAddr), .out(nextAdd));  // open: cin, cout
  // Probe on FLAGS_q[2]
  // Probe on FLAGS_q[3]
  // Probe on FLAGS_q[1]
  // Probe on FLAGS_q[0]
  not not_1 (not_1_out, FLAGS_q[0]);
  RAM #(.bus("separate")) ram_2 (
    .addr(op2_q), .din(A_2_q), .data(M), .str(st), .sel(1'b1), .clk(clk), .ld(1'b1));  // open: clr
  Multiplexer #(.select(2), .width(8), .enable("false")) multiplexer_10 (
    .in0(M), .in1(M), .in2(B_2_q), .in3(aluO), .out(EX), .sel(forwardsel_1_out_2));
  ForwardSel forwardsel_1 (.in_1(ctrl_2_q), .out_2(forwardsel_1_out_2));
  Multiplexer #(.select(2), .enable("false")) multiplexer_11 (
    .in0(hit_2_q), .in1(hit_2_q), .in2(hit_2_q), .in3(hit_2_q), .out(multiplexer_11_out), .sel(jmp));
  Multiplexer #(.select(2), .enable("false")) multiplexer_12 (
    .in0(1'b0), .in1(not_1_out), .in2(FLAGS_q[0]), .in3(FLAGS_q[1]), .out(j), .sel(jmp));
  and and_3 (aj, ~multiplexer_11_out, j);  // AND_Gate
  and and_4 (shj, multiplexer_11_out, ~j);  // AND_Gate
  Register op2_2 (.D(op2_q), .en(run), .Q(op2_2_q), .clk(clk), .clr(res));
  Register u_M (.D(M), .en(run), .Q(M_q), .clk(clk), .clr(res));
  Register ALUout_2 (.D(aluO), .en(run), .Q(ALUout_2_q), .clk(clk), .clr(res));
  Register B_3 (.D(B_2_q), .en(run), .Q(B_3_q), .clk(clk), .clr(res));
  Register #(.width(2)) dest_3 (.D(dest_2_q), .en(run), .Q(dest), .clk(clk), .clr(res));
  Register #(.width(3)) ctrl_3 (.D(ctrl_2_q), .en(run), .Q({wb_t, we}), .clk(clk), .clr(res));
  or or_4 (taken, aj, shj);
  Multiplexer #(.select(2), .width(8), .enable("false")) multiplexer_13 (
    .in0(M_q), .in1(M_q), .in2(B_3_q), .in3(ALUout_2_q), .out(MEM), .sel(forwardsel_2_out_2));
  ForwardSel forwardsel_2 (.in_1({wb_t, we}), .out_2(forwardsel_2_out_2));
  Multiplexer #(.select(2), .width(8), .enable("false")) multiplexer_14 (
    .in0(op2_2_q), .in1(M_q), .in2(ALUout_2_q), .in3(B_3_q), .out(data), .sel(wb_t));
  Register M_2 (.D(M_q), .en(run), .Q(M_2_q), .clk(clk), .clr(res));
  Register register_1 (.D(ALUout_2_q), .en(run), .Q(register_1_q), .clk(clk), .clr(res));
  Register register_2 (.D(B_3_q), .en(run), .Q(register_2_q), .clk(clk), .clr(res));
  Register #(.width(2)) register_3 (.D(dest), .en(run), .Q(oldD), .clk(clk), .clr(res));
  Register #(.width(3)) ctrl_4 (.D({wb_t, we}), .en(run), .Q({ctrl_4_q_2, ctrl_4_q[0]}), .clk(clk), .clr(res));
  Multiplexer #(.select(2), .width(8), .enable("false")) multiplexer_15 (
    .in0(M_2_q), .in1(M_2_q), .in2(register_2_q), .in3(register_1_q), .out(WB), .sel(forwardsel_3_out_2));
  ForwardSel forwardsel_3 (.in_1({ctrl_4_q_2, ctrl_4_q[0]}), .out_2(forwardsel_3_out_2));

  // Other names for the same wires on the sheet: R2[1:0] = p2[7:6]

  // Notes on the sheet:
  //   MIPS
  //    by Enrico Zelioli
  //   Instruction Memory
  //   Branch Unit
  //   Register File
  //   Control Unit
  //   Forwarding Unit
  //   ALU
  //   Data Memory
endmodule

module ALU1bit (
  input  Cin,
  input  [1:0] Sel,
  input  A,
  input  B,
  output O,
  output Cout
);

  wire adder_1_out, and_1_out, or_1_out, xor_1_out;

  xor xor_1 (xor_1_out, B, Sel[0]);
  and and_1 (and_1_out, A, B);
  or or_1 (or_1_out, A, B);
  Adder #(.width(1)) adder_1 (.a(A), .b(xor_1_out), .out(adder_1_out), .cin(Cin), .cout(Cout));
  Multiplexer #(.select(2), .enable("false")) multiplexer_1 (
    .in0(and_1_out), .in1(or_1_out), .in2(adder_1_out), .in3(adder_1_out), .out(O), .sel(Sel));

  // Other names for the same wires on the sheet: s[1:0] = Sel
endmodule

module ALU8bit (
  input  Cin,
  input  [1:0] Sel,
  input  [7:0] B,
  input  [7:0] A,
  output [7:0] ALUout,
  output [3:0] FLAGS
);

  wire alu1bit_1_cout, alu1bit_2_cout, alu1bit_3_cout, alu1bit_4_cout, alu1bit_5_cout, alu1bit_6_cout, Cout6;

  ALU1bit alu1bit_1 (.A(A[0]), .B(B[0]), .O(ALUout[0]), .Cin(Cin), .Sel(Sel), .Cout(alu1bit_1_cout));
  ALU1bit alu1bit_2 (.A(A[1]), .B(B[1]), .O(ALUout[1]), .Cin(alu1bit_1_cout), .Sel(Sel), .Cout(alu1bit_2_cout));
  ALU1bit alu1bit_3 (.A(A[2]), .B(B[2]), .O(ALUout[2]), .Cin(alu1bit_2_cout), .Sel(Sel), .Cout(alu1bit_3_cout));
  ALU1bit alu1bit_4 (.A(A[3]), .B(B[3]), .O(ALUout[3]), .Cin(alu1bit_3_cout), .Sel(Sel), .Cout(alu1bit_4_cout));
  ALU1bit alu1bit_5 (.A(A[4]), .B(B[4]), .O(ALUout[4]), .Cin(alu1bit_4_cout), .Sel(Sel), .Cout(alu1bit_5_cout));
  ALU1bit alu1bit_6 (.A(A[5]), .B(B[5]), .O(ALUout[5]), .Cin(alu1bit_5_cout), .Sel(Sel), .Cout(alu1bit_6_cout));
  ALU1bit alu1bit_7 (.A(A[6]), .B(B[6]), .O(ALUout[6]), .Cin(alu1bit_6_cout), .Sel(Sel), .Cout(Cout6));
  ALU1bit alu1bit_8 (.A(A[7]), .B(B[7]), .O(ALUout[7]), .Cin(Cout6), .Sel(Sel), .Cout(FLAGS[3]));
  xor xor_1 (FLAGS[2], Cout6, FLAGS[3]);
  nor nor_1 (FLAGS[0], ALUout[7], ALUout[6], ALUout[5], ALUout[4], ALUout[3], ALUout[2], ALUout[1], ALUout[0]);

  assign FLAGS[1] = ALUout[7];

  // Notes on the sheet:
  //   C O S Z
endmodule

module ControlUnit (
  input  [7:0] opcode,
  output [11:0] out_2
);

  flagie flagie_1 (.opcode(opcode), .flagie(out_2[0]));
  imm imm_1 (.opcode(opcode), .imm(out_2[1]));
  zero zero_1 (.opcode(opcode), .zero(out_2[2]));
  cin cin_1 (.opcode(opcode), .cin(out_2[3]));
  sel sel_1 (.opcode(opcode), .s1(out_2[5]), .s0(out_2[4]));
  jmp jmp_1 (.opcode(opcode), .jmp1(out_2[7]), .jmp2(out_2[6]));
  memst memst_1 (.opcode(opcode), .mst(out_2[8]));
  we we_1 (.opcode(opcode), .we(out_2[9]));
  wb wb_1 (.opcode(opcode), .wb1(out_2[11]), .wb0(out_2[10]));

  // Notes on the sheet:
  //   FLAGie
  //   imm
  //   zero
  //   Cin
  //   sel
  //   jmp
  //   memst
  //   we
  //   wb
endmodule

module RegisterSet (
  input  [7:0] DataIn,
  input  [1:0] dest,
  input  [1:0] R1sel,
  input  WE,
  input  [1:0] R2sel,
  input  clk,
  input  Reset,
  output [7:0] AL,
  output [7:0] BL,
  output [7:0] CL,
  output [7:0] DL,
  output [7:0] R1,
  output [7:0] R2
);

  wire demultiplexer_1_out0, demultiplexer_1_out1, demultiplexer_1_out2, demultiplexer_1_out3;

  Demultiplexer #(.select(2), .enable("false")) demultiplexer_1 (
    .out0(demultiplexer_1_out0), .out1(demultiplexer_1_out1), .out2(demultiplexer_1_out2),
    .out3(demultiplexer_1_out3), .in(WE), .sel(dest));
  Register u_AL (.D(DataIn), .en(demultiplexer_1_out0), .Q(AL), .clk(clk), .clr(Reset));
  Register u_BL (.D(DataIn), .en(demultiplexer_1_out1), .Q(BL), .clk(clk), .clr(Reset));
  Register u_CL (.D(DataIn), .en(demultiplexer_1_out2), .Q(CL), .clk(clk), .clr(Reset));
  Register u_DL (.D(DataIn), .en(demultiplexer_1_out3), .Q(DL), .clk(clk), .clr(Reset));
  Multiplexer #(.select(2), .width(8), .enable("false")) multiplexer_1 (
    .in0(AL), .in1(BL), .in2(CL), .in3(DL), .out(R1), .sel(R1sel));
  Multiplexer #(.select(2), .width(8), .enable("false")) multiplexer_2 (
    .in0(AL), .in1(BL), .in2(CL), .in3(DL), .out(R2), .sel(R2sel));
endmodule

module ForwardingUnit (
  input  [1:0] R1,
  input  [1:0] R2,
  input  zero,
  input  imm,
  input  [1:0] wb1,
  input  [1:0] dest1,
  input  we1,
  input  [1:0] wb2,
  input  [1:0] dest2,
  input  we2,
  input  [1:0] wb3,
  input  [1:0] dest3,
  input  we3,
  output [1:0] fA,
  output [1:0] fB
);

  wire and_1_out, and_2_out, and_3_out, and_4_out, and_5_out, and_6_out, and_13_out, and_14_out,
       comparator_1_eq, comparator_2_eq, comparator_3_eq, comparator_4_eq, comparator_5_eq, comparator_6_eq,
       comparator_7_eq, comparator_8_eq, comparator_9_eq, fA1, fA2, fA3, fB1, fB2, fB3, or_1_out, or_2_out;

  Comparator #(.width(2)) comparator_1 (.a(R1), .b(dest1), .eq(comparator_1_eq));  // open: gt, lt
  Comparator #(.width(2)) comparator_2 (.a(dest1), .b(R2), .eq(comparator_2_eq));  // open: gt, lt
  Comparator #(.width(2)) comparator_3 (.a(R1), .b(dest2), .eq(comparator_3_eq));  // open: gt, lt
  Comparator #(.width(2)) comparator_4 (.a(dest2), .b(R2), .eq(comparator_4_eq));  // open: gt, lt
  Comparator #(.width(2)) comparator_5 (.a(R1), .b(dest3), .eq(comparator_5_eq));  // open: gt, lt
  Comparator #(.width(2)) comparator_6 (.a(dest3), .b(R2), .eq(comparator_6_eq));  // open: gt, lt
  Comparator #(.width(2)) comparator_7 (.a(wb1), .b(2'b00), .eq(comparator_7_eq));  // open: gt, lt
  Comparator #(.width(2)) comparator_8 (.a(wb2), .b(2'b00), .eq(comparator_8_eq));  // open: gt, lt
  Comparator #(.width(2)) comparator_9 (.a(wb3), .b(2'b00), .eq(comparator_9_eq));  // open: gt, lt
  and and_1 (and_1_out, ~zero, comparator_1_eq);  // AND_Gate
  and and_2 (and_2_out, comparator_2_eq, ~imm);  // AND_Gate
  and and_3 (and_3_out, ~zero, comparator_3_eq);  // AND_Gate
  and and_4 (and_4_out, comparator_4_eq, ~imm);  // AND_Gate
  and and_5 (and_5_out, ~zero, comparator_5_eq);  // AND_Gate
  and and_6 (and_6_out, comparator_6_eq, ~imm);  // AND_Gate
  and and_7 (fA1, and_1_out, we1, ~comparator_7_eq);  // AND_Gate
  and and_8 (fB1, ~comparator_7_eq, we1, and_2_out);  // AND_Gate
  and and_9 (fA2, and_3_out, we2, ~comparator_8_eq);  // AND_Gate
  and and_10 (fB2, ~comparator_8_eq, we2, and_4_out);  // AND_Gate
  and and_11 (fA3, and_5_out, we3, ~comparator_9_eq);  // AND_Gate
  and and_12 (fB3, ~comparator_9_eq, we3, and_6_out);  // AND_Gate
  and and_13 (and_13_out, ~fA2, fA3);  // AND_Gate
  or or_1 (or_1_out, fA2, fA3);
  and and_14 (and_14_out, ~fB2, fB3);  // AND_Gate
  or or_2 (or_2_out, fB2, fB3);
  or or_3 (fA[0], fA1, and_13_out);
  and and_15 (fA[1], ~fA1, or_1_out);  // AND_Gate
  nor nor_1 (fB[0], fB1, and_14_out);
  nand nand_1 (fB[1], ~fB1, or_2_out);  // NAND_Gate
endmodule

module ForwardSel (
  input  [2:0] in_1,
  output [1:0] out_2
);

  wire comparator_1_eq;

  Comparator #(.width(2)) comparator_1 (.a(in_1[2:1]), .b(2'b01), .eq(comparator_1_eq));  // open: gt, lt
  not not_1 (out_2[0], in_1[1]);
  not not_2 (out_2[1], comparator_1_eq);
endmodule

module BranchUnit (
  input  [7:0] pc,
  input  res,
  input  clk,
  input  update,
  input  [15:0] in_5,
  input  [1:0] jmp,
  input  [7:0] op,
  input  [7:0] jr,
  output hit,
  output [7:0] address,
  output out_11,
  output out_12
);

  wire and_1_out, and_2_out, and_3_out, and_4_out, and_5_out, and_6_out, and_7_out, and_8_out,
       comparator_3_eq, comparator_4_eq, comparator_5_eq, comparator_6_eq, en1, en2, en3, en4, nor_1_out,
       or_1_out;
  wire [7:0] a1, a2, a3, a4;
  wire [16:0] register_1_q, register_2_q, register_3_q, register_4_q;

  or or_1 (or_1_out, jmp[0], jmp[1]);
  Demultiplexer #(.select(2), .enable("false")) demultiplexer_1 (
    .out0(en1), .out1(en2), .out2(en3), .out3(en4), .in(or_1_out), .sel(in_5[1:0]));
  Comparator comparator_1 (.a(8'h13), .b(op), .eq(out_11));  // open: gt, lt
  Comparator comparator_2 (.a(8'h17), .b(jr), .eq(out_12));  // open: gt, lt
  Register #(.width(17)) register_1 (
    .D({update, in_5}), .en(en1), .Q({register_1_q[16], a1, register_1_q[7:0]}), .clk(clk), .clr(res));
  Register #(.width(17)) register_2 (
    .D({update, in_5}), .en(en2), .Q({register_2_q[16], a2, register_2_q[7:0]}), .clk(clk), .clr(res));
  Register #(.width(17)) register_3 (
    .D({update, in_5}), .en(en3), .Q({register_3_q[16], a3, register_3_q[7:0]}), .clk(clk), .clr(res));
  Register #(.width(17)) register_4 (
    .D({update, in_5}), .en(en4), .Q({register_4_q[16], a4, register_4_q[7:0]}), .clk(clk), .clr(res));
  Comparator comparator_3 (.a(pc), .b(register_1_q[7:0]), .eq(comparator_3_eq));  // open: gt, lt
  Comparator comparator_4 (.a(pc), .b(register_2_q[7:0]), .eq(comparator_4_eq));  // open: gt, lt
  Comparator comparator_5 (.a(pc), .b(register_3_q[7:0]), .eq(comparator_5_eq));  // open: gt, lt
  Comparator comparator_6 (.a(pc), .b(register_4_q[7:0]), .eq(comparator_6_eq));  // open: gt, lt
  and and_1 (and_1_out, comparator_3_eq, register_1_q[16]);
  and and_2 (and_2_out, comparator_4_eq, register_2_q[16]);
  and and_3 (and_3_out, comparator_5_eq, register_3_q[16]);
  and and_4 (and_4_out, comparator_6_eq, register_4_q[16]);
  or or_2 (hit, and_1_out, and_2_out, and_3_out, and_4_out);
  and and_5 (and_5_out, ~and_4_out, ~and_3_out, ~and_2_out, and_1_out);  // AND_Gate
  and and_6 (and_6_out, ~and_4_out, ~and_3_out, and_2_out, ~and_1_out);  // AND_Gate
  and and_7 (and_7_out, ~and_4_out, and_3_out, ~and_2_out, ~and_1_out);  // AND_Gate
  and and_8 (and_8_out, and_4_out, ~and_3_out, ~and_2_out, ~and_1_out);  // AND_Gate
  nor nor_1 (nor_1_out, and_5_out, and_6_out, and_7_out, and_8_out);
  assign address = and_5_out ? a1 : 8'bz;  // Controlled_Buffer controlled_buffer_1
  assign address = and_6_out ? a2 : 8'bz;  // Controlled_Buffer controlled_buffer_2
  assign address = and_7_out ? a3 : 8'bz;  // Controlled_Buffer controlled_buffer_3
  assign address = and_8_out ? a4 : 8'bz;  // Controlled_Buffer controlled_buffer_4
  assign address = nor_1_out ? {8{1'b0}} : 8'bz;  // Controlled_Buffer controlled_buffer_5
endmodule

module wb (
  input  [7:0] opcode,
  output wb1,
  output wb0
);

  wire and_1_out, and_2_out, and_3_out, and_4_out, and_5_out, and_6_out, and_7_out, and_8_out, and_9_out,
       and_10_out, and_11_out, and_12_out, and_13_out, and_14_out, and_15_out;

  and and_1 (and_1_out, ~opcode[4], ~opcode[3], ~opcode[2], ~opcode[1], opcode[0]);  // AND_Gate
  and and_2 (and_2_out, ~opcode[4], ~opcode[3], opcode[2], ~opcode[1], opcode[0]);  // AND_Gate
  and and_3 (and_3_out, ~opcode[4], ~opcode[3], opcode[2], opcode[1], ~opcode[0]);  // AND_Gate
  and and_4 (and_4_out, ~opcode[4], ~opcode[3], opcode[2], opcode[1], opcode[0]);  // AND_Gate
  and and_5 (and_5_out, ~opcode[4], opcode[3], ~opcode[2], ~opcode[1], opcode[0]);  // AND_Gate
  and and_6 (and_6_out, ~opcode[4], opcode[3], ~opcode[2], opcode[1], ~opcode[0]);  // AND_Gate
  and and_7 (and_7_out, ~opcode[4], opcode[3], opcode[2], ~opcode[1], ~opcode[0]);  // AND_Gate
  and and_8 (and_8_out, ~opcode[4], opcode[3], opcode[2], ~opcode[1], opcode[0]);  // AND_Gate
  and and_9 (and_9_out, ~opcode[4], opcode[3], opcode[2], opcode[1], opcode[0]);  // AND_Gate
  and and_10 (and_10_out, opcode[4], ~opcode[3], ~opcode[2], ~opcode[1], ~opcode[0]);  // AND_Gate
  and and_11 (and_11_out, opcode[4], ~opcode[3], ~opcode[2], opcode[1], ~opcode[0]);  // AND_Gate
  and and_12 (and_12_out, ~opcode[4], ~opcode[3], ~opcode[2], opcode[1], opcode[0]);  // AND_Gate
  and and_13 (and_13_out, ~opcode[4], ~opcode[3], ~opcode[2], ~opcode[1], opcode[0]);  // AND_Gate
  and and_14 (and_14_out, ~opcode[4], ~opcode[3], ~opcode[2], opcode[1], ~opcode[0]);  // AND_Gate
  and and_15 (and_15_out, ~opcode[4], ~opcode[3], opcode[2], ~opcode[1], opcode[0]);  // AND_Gate
  or or_1 (wb1, and_1_out, and_2_out, and_3_out, and_4_out, and_5_out, and_6_out, and_7_out, and_8_out, and_9_out, and_10_out, and_11_out);
  or or_2 (wb0, and_13_out, and_14_out, and_15_out);
endmodule

module we (
  input  [7:0] opcode,
  output we
);

  wire and_1_out, and_2_out, and_3_out, and_4_out, and_5_out, and_6_out, and_7_out, and_8_out, and_9_out,
       and_10_out, and_11_out, and_12_out;

  and and_1 (and_1_out, ~opcode[4], ~opcode[3], ~opcode[2], ~opcode[1], opcode[0]);  // AND_Gate
  and and_2 (and_2_out, ~opcode[4], ~opcode[3], ~opcode[2], opcode[1], ~opcode[0]);  // AND_Gate
  and and_3 (and_3_out, ~opcode[4], ~opcode[3], opcode[2], ~opcode[1], opcode[0]);  // AND_Gate
  and and_4 (and_4_out, ~opcode[4], ~opcode[3], opcode[2], opcode[1], ~opcode[0]);  // AND_Gate
  and and_5 (and_5_out, ~opcode[4], ~opcode[3], opcode[2], opcode[1], opcode[0]);  // AND_Gate
  and and_6 (and_6_out, ~opcode[4], opcode[3], ~opcode[2], ~opcode[1], opcode[0]);  // AND_Gate
  and and_7 (and_7_out, ~opcode[4], opcode[3], ~opcode[2], opcode[1], ~opcode[0]);  // AND_Gate
  and and_8 (and_8_out, ~opcode[4], opcode[3], opcode[2], ~opcode[1], ~opcode[0]);  // AND_Gate
  and and_9 (and_9_out, ~opcode[4], opcode[3], opcode[2], ~opcode[1], opcode[0]);  // AND_Gate
  and and_10 (and_10_out, ~opcode[4], opcode[3], opcode[2], opcode[1], opcode[0]);  // AND_Gate
  and and_11 (and_11_out, opcode[4], ~opcode[3], ~opcode[2], ~opcode[1], ~opcode[0]);  // AND_Gate
  and and_12 (and_12_out, opcode[4], ~opcode[3], ~opcode[2], ~opcode[1], opcode[0]);  // AND_Gate
  or or_1 (we, and_1_out, and_2_out, and_3_out, and_4_out, and_5_out, and_6_out, and_7_out, and_8_out, and_9_out, and_10_out, and_11_out, and_12_out);
endmodule

module memst (
  input  [7:0] opcode,
  output mst
);

  and and_1 (mst, ~opcode[4], ~opcode[3], ~opcode[2], opcode[1], opcode[0]);  // AND_Gate
endmodule

module jmp (
  input  [7:0] opcode,
  output jmp1,
  output jmp2
);

  wire and_1_out, and_2_out, and_3_out;

  and and_1 (and_1_out, opcode[4], ~opcode[3], opcode[2], ~opcode[1], ~opcode[0]);  // AND_Gate
  and and_2 (and_2_out, opcode[4], ~opcode[3], opcode[2], ~opcode[1], opcode[0]);  // AND_Gate
  and and_3 (and_3_out, opcode[4], ~opcode[3], opcode[2], opcode[1], ~opcode[0]);  // AND_Gate
  or or_1 (jmp1, and_1_out, and_2_out);
  or or_2 (jmp2, and_2_out, and_3_out);
endmodule

module sel (
  input  [7:0] opcode,
  output s1,
  output s0
);

  wire and_1_out, and_2_out, and_3_out, and_4_out, and_5_out, and_6_out, and_7_out, and_8_out, and_9_out,
       and_10_out, and_11_out, and_12_out, and_13_out, and_14_out, and_15_out;

  and and_1 (and_1_out, opcode[4], opcode[3], ~opcode[2], ~opcode[1], opcode[0]);  // AND_Gate
  and and_2 (and_2_out, ~opcode[4], ~opcode[3], opcode[2], opcode[1], ~opcode[0]);  // AND_Gate
  and and_3 (and_3_out, ~opcode[4], ~opcode[3], opcode[2], opcode[1], opcode[0]);  // AND_Gate
  and and_4 (and_4_out, ~opcode[4], opcode[3], ~opcode[2], ~opcode[1], opcode[0]);  // AND_Gate
  and and_5 (and_5_out, ~opcode[4], opcode[3], ~opcode[2], opcode[1], ~opcode[0]);  // AND_Gate
  and and_6 (and_6_out, opcode[4], ~opcode[3], ~opcode[2], opcode[1], ~opcode[0]);  // AND_Gate
  and and_7 (and_7_out, opcode[4], opcode[3], ~opcode[2], ~opcode[1], ~opcode[0]);  // AND_Gate
  and and_8 (and_8_out, ~opcode[4], opcode[3], ~opcode[2], ~opcode[1], opcode[0]);  // AND_Gate
  and and_9 (and_9_out, ~opcode[4], opcode[3], ~opcode[2], opcode[1], ~opcode[0]);  // AND_Gate
  and and_10 (and_10_out, ~opcode[4], opcode[3], opcode[2], opcode[1], opcode[0]);  // AND_Gate
  and and_11 (and_11_out, opcode[4], ~opcode[3], ~opcode[2], ~opcode[1], ~opcode[0]);  // AND_Gate
  and and_12 (and_12_out, opcode[4], ~opcode[3], ~opcode[2], opcode[1], ~opcode[0]);  // AND_Gate
  and and_13 (and_13_out, opcode[4], opcode[3], ~opcode[2], ~opcode[1], ~opcode[0]);  // AND_Gate
  and and_14 (and_14_out, opcode[4], opcode[3], ~opcode[2], ~opcode[1], ~opcode[0]);  // AND_Gate
  and and_15 (and_15_out, opcode[4], opcode[3], ~opcode[2], ~opcode[1], opcode[0]);  // AND_Gate
  or or_1 (s1, and_1_out, and_2_out, and_3_out, and_4_out, and_5_out, and_6_out, and_7_out);
  or or_2 (s0, and_8_out, and_9_out, and_10_out, and_11_out, and_12_out, and_13_out, and_14_out, and_15_out);
endmodule

module cin (
  input  [7:0] opcode,
  output cin
);

  wire and_1_out, and_2_out, and_3_out, and_4_out;

  and and_1 (and_1_out, ~opcode[4], opcode[3], ~opcode[2], ~opcode[1], opcode[0]);  // AND_Gate
  and and_2 (and_2_out, ~opcode[4], opcode[3], ~opcode[2], opcode[1], ~opcode[0]);  // AND_Gate
  and and_3 (and_3_out, opcode[4], opcode[3], ~opcode[2], ~opcode[1], ~opcode[0]);  // AND_Gate
  and and_4 (and_4_out, opcode[4], opcode[3], ~opcode[2], ~opcode[1], opcode[0]);  // AND_Gate
  or or_1 (cin, and_1_out, and_2_out, and_3_out, and_4_out);
endmodule

module zero (
  input  [7:0] opcode,
  output zero
);

  wire and_1_out, and_2_out;

  and and_1 (and_1_out, ~opcode[4], ~opcode[3], ~opcode[2], opcode[1], opcode[0]);  // AND_Gate
  and and_2 (and_2_out, opcode[4], ~opcode[3], ~opcode[2], opcode[1], ~opcode[0]);  // AND_Gate
  buf or_1 (zero, and_2_out);  // OR_Gate
endmodule

module imm (
  input  [7:0] opcode,
  output imm
);

  wire and_1_out, and_2_out, and_3_out, and_4_out, and_5_out, and_6_out, and_7_out;

  and and_1 (and_1_out, ~opcode[4], ~opcode[3], ~opcode[2], ~opcode[1], opcode[0]);  // AND_Gate
  and and_2 (and_2_out, ~opcode[4], ~opcode[3], opcode[2], opcode[1], opcode[0]);  // AND_Gate
  and and_3 (and_3_out, ~opcode[4], opcode[3], ~opcode[2], opcode[1], ~opcode[0]);  // AND_Gate
  and and_4 (and_4_out, ~opcode[4], opcode[3], opcode[2], ~opcode[1], opcode[0]);  // AND_Gate
  and and_5 (and_5_out, opcode[4], ~opcode[3], ~opcode[2], ~opcode[1], ~opcode[0]);  // AND_Gate
  and and_6 (and_6_out, opcode[4], ~opcode[3], ~opcode[2], opcode[1], ~opcode[0]);  // AND_Gate
  and and_7 (and_7_out, opcode[4], opcode[3], ~opcode[2], ~opcode[1], ~opcode[0]);  // AND_Gate
  or or_1 (imm, and_1_out, and_2_out, and_3_out, and_4_out, and_5_out, and_6_out, and_7_out);
endmodule

module flagie (
  input  [7:0] opcode,
  output flagie
);

  wire and_1_out, and_2_out, and_3_out, and_4_out, and_5_out, and_6_out, and_7_out, and_8_out, and_9_out,
       and_10_out, and_11_out, and_12_out, and_13_out, and_14_out, and_15_out;

  and and_1 (and_1_out, ~opcode[4], ~opcode[3], opcode[2], opcode[1], ~opcode[0]);  // AND_Gate
  and and_2 (and_2_out, ~opcode[4], ~opcode[3], opcode[2], opcode[1], opcode[0]);  // AND_Gate
  and and_3 (and_3_out, ~opcode[4], opcode[3], ~opcode[2], ~opcode[1], ~opcode[0]);  // AND_Gate
  and and_4 (and_4_out, ~opcode[4], opcode[3], ~opcode[2], ~opcode[1], opcode[0]);  // AND_Gate
  and and_5 (and_5_out, ~opcode[4], opcode[3], ~opcode[2], opcode[1], ~opcode[0]);  // AND_Gate
  and and_6 (and_6_out, ~opcode[4], opcode[3], ~opcode[2], opcode[1], opcode[0]);  // AND_Gate
  and and_7 (and_7_out, ~opcode[4], opcode[3], opcode[2], ~opcode[1], ~opcode[0]);  // AND_Gate
  and and_8 (and_8_out, ~opcode[4], opcode[3], opcode[2], ~opcode[1], opcode[0]);  // AND_Gate
  and and_9 (and_9_out, ~opcode[4], opcode[3], opcode[2], opcode[1], ~opcode[0]);  // AND_Gate
  and and_10 (and_10_out, ~opcode[4], opcode[3], opcode[2], opcode[1], opcode[0]);  // AND_Gate
  and and_11 (and_11_out, opcode[4], ~opcode[3], ~opcode[2], ~opcode[1], ~opcode[0]);  // AND_Gate
  and and_12 (and_12_out, opcode[4], ~opcode[3], ~opcode[2], ~opcode[1], opcode[0]);  // AND_Gate
  and and_13 (and_13_out, opcode[4], ~opcode[3], ~opcode[2], opcode[1], ~opcode[0]);  // AND_Gate
  and and_14 (and_14_out, opcode[4], opcode[3], ~opcode[2], ~opcode[1], ~opcode[0]);  // AND_Gate
  and and_15 (and_15_out, opcode[4], opcode[3], ~opcode[2], ~opcode[1], opcode[0]);  // AND_Gate
  or or_1 (flagie, and_1_out, and_2_out, and_3_out, and_4_out, and_5_out, and_6_out, and_7_out, and_8_out, and_9_out, and_10_out, and_11_out, and_12_out, and_13_out, and_14_out, and_15_out);
endmodule
